// Logisim project EnhancedAlu.circ as structural Verilog: 23 circuits, main circuit oneBitAdder
module oneBitAdder (
  input  A1,
  input  B1,
  input  Cin,
  output S1,
  output Cout
);

  wire and_1_out, and_2_out, xor_1_out;

  xor xor_1 (xor_1_out, A1, B1);
  and and_1 (and_1_out, xor_1_out, Cin);
  and and_2 (and_2_out, A1, B1);
  xor xor_2 (S1, xor_1_out, Cin);
  or or_1 (Cout, and_1_out, and_2_out);
endmodule

module twoBitAdder (
  input  [1:0] A2,
  input  [1:0] B2,
  input  Cin,
  output [1:0] S2,
  output Cout
);

  wire onebitadder_1_cout;

  oneBitAdder onebitadder_1 (.A1(A2[0]), .B1(B2[0]), .Cin(Cin), .S1(S2[0]), .Cout(onebitadder_1_cout));
  oneBitAdder onebitadder_2 (.A1(A2[1]), .B1(B2[1]), .Cin(onebitadder_1_cout), .S1(S2[1]), .Cout(Cout));
endmodule

module fourBitAdder (
  input  [3:0] A4,
  input  [3:0] B4,
  input  Cin,
  output [3:0] S4,
  output Cout
);

  wire twobitadder_1_cout;

  twoBitAdder twobitadder_1 (.A2(A4[1:0]), .B2(B4[1:0]), .Cin(Cin), .S2(S4[1:0]), .Cout(twobitadder_1_cout));
  twoBitAdder twobitadder_2 (.A2(A4[3:2]), .B2(B4[3:2]), .Cin(twobitadder_1_cout), .S2(S4[3:2]), .Cout(Cout));
endmodule

module eightBitAdder (
  input  [7:0] A8,
  input  [7:0] B8,
  input  Cin,
  output [7:0] S8,
  output Cout
);

  wire fourbitadder_1_cout;

  fourBitAdder fourbitadder_1 (.A4(A8[3:0]), .B4(B8[3:0]), .Cin(Cin), .S4(S8[3:0]), .Cout(fourbitadder_1_cout));
  fourBitAdder fourbitadder_2 (.A4(A8[7:4]), .B4(B8[7:4]), .Cin(fourbitadder_1_cout), .S4(S8[7:4]), .Cout(Cout));
endmodule

module sixteenBitAdder (
  input  [15:0] A16,
  input  [15:0] B16,
  input  Cin,
  output [15:0] S16,
  output Cout
);

  wire eightbitadder_1_cout;

  eightBitAdder eightbitadder_1 (.A8(A16[7:0]), .B8(B16[7:0]), .Cin(Cin), .S8(S16[7:0]), .Cout(eightbitadder_1_cout));
  eightBitAdder eightbitadder_2 (
    .A8(A16[15:8]), .B8(B16[15:8]), .Cin(eightbitadder_1_cout), .S8(S16[15:8]), .Cout(Cout));
endmodule

module thirtytwoBitAdder (
  input  [31:0] A,
  input  [31:0] B,
  input  Cin,
  output [31:0] Result,
  output ZeroOutput
);

  wire eightbitadder_1_cout, fourbitadder_1_cout, onebitadder_1_cout, onebitadder_2_cout,
       sixteenbitadder_1_cout, twobitadder_1_cout;
  wire [31:0] multiplexer_1_out, not_1_out;

  assign not_1_out = ~B;  // NOT_Gate not_1, 32 bits wide
  Multiplexer #(.enable("false"), .width(32)) multiplexer_1 (
    .in0(B), .in1(not_1_out), .out(multiplexer_1_out), .sel(Cin));
  sixteenBitAdder sixteenbitadder_1 (
    .A16(A[15:0]), .B16(multiplexer_1_out[15:0]), .Cin(Cin), .S16(Result[15:0]), .Cout(sixteenbitadder_1_cout));
  eightBitAdder eightbitadder_1 (
    .A8(A[23:16]), .B8(multiplexer_1_out[23:16]), .Cin(sixteenbitadder_1_cout), .S8(Result[23:16]),
    .Cout(eightbitadder_1_cout));
  fourBitAdder fourbitadder_1 (
    .A4(A[27:24]), .B4(multiplexer_1_out[27:24]), .Cin(eightbitadder_1_cout), .S4(Result[27:24]),
    .Cout(fourbitadder_1_cout));
  twoBitAdder twobitadder_1 (
    .A2(A[29:28]), .B2(multiplexer_1_out[29:28]), .Cin(fourbitadder_1_cout), .S2(Result[29:28]),
    .Cout(twobitadder_1_cout));
  oneBitAdder onebitadder_1 (
    .A1(A[30]), .B1(multiplexer_1_out[30]), .Cin(twobitadder_1_cout), .S1(Result[30]),
    .Cout(onebitadder_1_cout));
  oneBitAdder onebitadder_2 (
    .A1(A[31]), .B1(multiplexer_1_out[31]), .Cin(onebitadder_1_cout), .S1(Result[31]),
    .Cout(onebitadder_2_cout));
  xor xor_1 (ZeroOutput, onebitadder_1_cout, onebitadder_2_cout);
endmodule

module oneBitShift (
  input  Cin,
  input  [31:0] shift,
  input  shiftEnable,
  output [31:0] shiftResult
);

  Multiplexer #(.enable("false"), .width(32)) multiplexer_1 (
    .in0(shift), .in1({shift[30:0], Cin}), .out(shiftResult), .sel(shiftEnable));
endmodule

module twoBitShift (
  input  Cin,
  input  [31:0] shift,
  input  shiftEnable,
  output [31:0] shiftResult
);

  Multiplexer #(.enable("false"), .width(32)) multiplexer_1 (
    .in0(shift), .in1({shift[29:0], {2{Cin}}}), .out(shiftResult), .sel(shiftEnable));
endmodule

module fourBitShift (
  input  Cin,
  input  [31:0] shift,
  input  shiftEnable,
  output [31:0] shiftResult
);

  Multiplexer #(.enable("false"), .width(32)) multiplexer_1 (
    .in0(shift), .in1({shift[27:0], {4{Cin}}}), .out(shiftResult), .sel(shiftEnable));
endmodule

module eightBitShift (
  input  Cin,
  input  [31:0] shift,
  input  shiftEnable,
  output [31:0] shiftResult
);

  Multiplexer #(.enable("false"), .width(32)) multiplexer_1 (
    .in0(shift), .in1({shift[23:0], {8{Cin}}}), .out(shiftResult), .sel(shiftEnable));
endmodule

module sixteenBitShift (
  input  Cin,
  input  [31:0] shift,
  input  shiftEnable,
  output [31:0] shiftResult
);

  Multiplexer #(.enable("false"), .width(32)) multiplexer_1 (
    .in0(shift), .in1({shift[15:0], {16{Cin}}}), .out(shiftResult), .sel(shiftEnable));
endmodule

module logicalLeftShift32 (
  input  Cin,
  input  [31:0] B,
  input  [4:0] shiftAmount,
  output [31:0] Result
);

  wire [31:0] eightbitshift_1_shiftresult, fourbitshift_1_shiftresult, onebitshift_1_shiftresult,
       twobitshift_1_shiftresult;

  oneBitShift onebitshift_1 (
    .Cin(Cin), .shift(B), .shiftEnable(shiftAmount[0]), .shiftResult(onebitshift_1_shiftresult));
  twoBitShift twobitshift_1 (
    .Cin(Cin), .shift(onebitshift_1_shiftresult), .shiftEnable(shiftAmount[1]),
    .shiftResult(twobitshift_1_shiftresult));
  fourBitShift fourbitshift_1 (
    .Cin(Cin), .shift(twobitshift_1_shiftresult), .shiftEnable(shiftAmount[2]),
    .shiftResult(fourbitshift_1_shiftresult));
  eightBitShift eightbitshift_1 (
    .Cin(Cin), .shift(fourbitshift_1_shiftresult), .shiftEnable(shiftAmount[3]),
    .shiftResult(eightbitshift_1_shiftresult));
  sixteenBitShift sixteenbitshift_1 (
    .Cin(Cin), .shift(eightbitshift_1_shiftresult), .shiftEnable(shiftAmount[4]), .shiftResult(Result));
endmodule

module bitReversal32 (
  input  [31:0] bitInsert,
  output [31:0] Result
);


  assign Result = {bitInsert[0], bitInsert[1], bitInsert[2], bitInsert[3], bitInsert[4], bitInsert[5], bitInsert[6], bitInsert[7], bitInsert[8], bitInsert[9], bitInsert[10], bitInsert[11], bitInsert[12], bitInsert[13], bitInsert[14], bitInsert[15], bitInsert[16], bitInsert[17], bitInsert[18], bitInsert[19], bitInsert[20], bitInsert[21], bitInsert[22], bitInsert[23], bitInsert[24], bitInsert[25], bitInsert[26], bitInsert[27], bitInsert[28], bitInsert[29], bitInsert[30], bitInsert[31]};
endmodule

module logicalRightShift (
  input  [31:0] B,
  input  Cin,
  input  [4:0] shiftAmount,
  output [31:0] out_4
);

  wire [31:0] bitreversal32_1_result, logicalleftshift32_1_result;

  bitReversal32 bitreversal32_1 (.bitInsert(B), .Result(bitreversal32_1_result));
  logicalLeftShift32 logicalleftshift32_1 (
    .Cin(Cin), .B(bitreversal32_1_result), .shiftAmount(shiftAmount), .Result(logicalleftshift32_1_result));
  bitReversal32 bitreversal32_2 (.bitInsert(logicalleftshift32_1_result), .Result(out_4));
endmodule

module greaterLessComparator (
  input  [31:0] A,
  output out_2
);

  wire nor_1_out;

  nor nor_1 (nor_1_out, A[0], A[1], A[2], A[3], A[4], A[5], A[6], A[7], A[8], A[9], A[10], A[11], A[12], A[13], A[14], A[15], A[16], A[17], A[18], A[19], A[20], A[21], A[22], A[23], A[24], A[25], A[26], A[27], A[28], A[29], A[30], A[31]);
  or or_1 (out_2, A[31], nor_1_out);
endmodule

module equalsComparator (
  input  [31:0] A,
  input  [31:0] B,
  output equalsOut
);

  wire [31:0] nor_1_out;

  assign nor_1_out = ~(A | B);  // NOR_Gate nor_1, 32 bits wide
  and and_1 (equalsOut, nor_1_out[0], nor_1_out[1], nor_1_out[2], nor_1_out[3], nor_1_out[4], nor_1_out[5], nor_1_out[6], nor_1_out[7], nor_1_out[8], nor_1_out[9], nor_1_out[10], nor_1_out[11], nor_1_out[12], nor_1_out[13], nor_1_out[14], nor_1_out[15], nor_1_out[16], nor_1_out[17], nor_1_out[18], nor_1_out[19], nor_1_out[20], nor_1_out[21], nor_1_out[22], nor_1_out[23], nor_1_out[24], nor_1_out[25], nor_1_out[26], nor_1_out[27], nor_1_out[28], nor_1_out[29], nor_1_out[30], nor_1_out[31]);
endmodule

module shiftRight32CinCirc (
  input  [31:0] B,
  input  [4:0] shiftAmount,
  output [31:0] Result
);

  wire [31:0] bitreversal32_1_result, logicalleftshift32_1_result;

  bitReversal32 bitreversal32_1 (.bitInsert(B), .Result(bitreversal32_1_result));
  logicalLeftShift32 logicalleftshift32_1 (
    .Cin(B[31]), .B(bitreversal32_1_result), .shiftAmount(shiftAmount), .Result(logicalleftshift32_1_result));
  bitReversal32 bitreversal32_2 (.bitInsert(logicalleftshift32_1_result), .Result(Result));
endmodule

module EquivalencesLogic (
  input  [31:0] A,
  input  [31:0] B,
  input  [1:0] OpIn,
  output Result
);

  wire equalscomparator_1_equalsout, equalscomparator_2_equalsout, greaterlesscomparator_1_out_2,
       greaterlesscomparator_2_out_2, not_1_out, not_2_out;

  equalsComparator equalscomparator_1 (.A(A), .B(B), .equalsOut(equalscomparator_1_equalsout));
  equalsComparator equalscomparator_2 (.A(A), .B(B), .equalsOut(equalscomparator_2_equalsout));
  greaterLessComparator greaterlesscomparator_1 (.A(A), .out_2(greaterlesscomparator_1_out_2));
  greaterLessComparator greaterlesscomparator_2 (.A(A), .out_2(greaterlesscomparator_2_out_2));
  not not_1 (not_1_out, equalscomparator_1_equalsout);
  not not_2 (not_2_out, greaterlesscomparator_2_out_2);
  Multiplexer #(.enable("false"), .select(2)) multiplexer_1 (
    .in0(not_1_out), .in1(equalscomparator_2_equalsout), .in2(greaterlesscomparator_1_out_2),
    .in3(not_2_out), .out(Result), .sel(OpIn));
endmodule

module directOpsLogic (
  input  [31:0] A,
  input  [31:0] B,
  input  [1:0] shiftAmount,
  output [31:0] Result
);

  wire [31:0] and_1_out, nor_1_out, or_1_out, xor_1_out;

  assign and_1_out = B & A;  // AND_Gate and_1, 32 bits wide
  assign or_1_out = B | A;  // OR_Gate or_1, 32 bits wide
  assign xor_1_out = B ^ A;  // XOR_Gate xor_1, 32 bits wide
  assign nor_1_out = ~(B | A);  // NOR_Gate nor_1, 32 bits wide
  Multiplexer #(.enable("false"), .select(2), .width(32)) multiplexer_1 (
    .in0(and_1_out), .in1(or_1_out), .in2(xor_1_out), .in3(nor_1_out), .out(Result), .sel(shiftAmount));
endmodule

module ArithmeticWithShiftLogic (
  input  Cin,
  input  [31:0] B,
  input  [31:0] A,
  input  [4:0] shiftAmount,
  input  [2:0] OpIn,
  output [31:0] Result,
  output Overflowflag
);

  wire intmul_1_overflow, or_1_out, thirtytwobitadder_1_zerooutput;
  wire [31:0] intmul_1_result, logicalleftshift32_1_result, logicalrightshift_1_out_4,
       shiftright32cincirc_1_result, thirtytwobitadder_1_result;

  logicalLeftShift32 logicalleftshift32_1 (
    .Cin(Cin), .B(B), .shiftAmount(shiftAmount), .Result(logicalleftshift32_1_result));
  logicalRightShift logicalrightshift_1 (
    .B(B), .Cin(Cin), .shiftAmount(shiftAmount), .out_4(logicalrightshift_1_out_4));
  shiftRight32CinCirc shiftright32cincirc_1 (.B(B), .shiftAmount(shiftAmount), .Result(shiftright32cincirc_1_result));
  IntMul intmul_1 (.Ain(A), .Bin(B), .result(intmul_1_result), .Overflow(intmul_1_overflow));
  // Probe on logicalleftshift32_1_result
  thirtytwoBitAdder thirtytwobitadder_1 (
    .A(A), .B(B), .Cin(OpIn[2]), .Result(thirtytwobitadder_1_result),
    .ZeroOutput(thirtytwobitadder_1_zerooutput));
  or or_1 (or_1_out, thirtytwobitadder_1_zerooutput, intmul_1_overflow);
  Multiplexer #(.enable("false"), .select(3), .width(32)) multiplexer_1 (
    .in0(logicalleftshift32_1_result), .in1(logicalleftshift32_1_result), .in2(thirtytwobitadder_1_result),
    .in3(thirtytwobitadder_1_result), .in4(logicalrightshift_1_out_4), .in5(shiftright32cincirc_1_result),
    .in6(intmul_1_result), .in7(thirtytwobitadder_1_result), .out(Result), .sel(OpIn));
  and and_1 (Overflowflag, OpIn[1], or_1_out);
endmodule

module VectorALU (
  input  [31:0] X0,
  input  [31:0] Y0,
  input  [31:0] X1,
  input  [31:0] Y1,
  input  [4:0] shiftAmount,
  input  [3:0] Op,
  input  ClearRegisters,
  output [31:0] out_8,
  output [31:0] out_9,
  output [31:0] out_10,
  output [31:0] out_11
);

  wire clock_1_out;
  wire [31:0] X0X1ALU_result, X0Y0ALU_result, X1Y1ALU_result, Y0Y1ALU_result;
  wire [63:0] X0Y0_q, X1Y1_q;

  Clock clock_1 (.out(clock_1_out));
  Register #(.width(64)) X0Y0 (.D({Y0, X0}), .clk(clock_1_out), .Q(X0Y0_q), .clr(ClearRegisters));  // open: en
  Register #(.width(64)) X1Y1 (.D({Y1, X1}), .clk(clock_1_out), .Q(X1Y1_q), .clr(ClearRegisters));  // open: en
  thirtyTwoBitALU X0Y0ALU (
    .A(X0Y0_q[31:0]), .B(X0Y0_q[63:32]), .Opcode(Op), .shiftAmount(shiftAmount), .Result(X0Y0ALU_result));  // open: ErrorBit
  thirtyTwoBitALU X0X1ALU (
    .A(X0Y0_q[31:0]), .B(X1Y1_q[31:0]), .Opcode(Op), .shiftAmount(shiftAmount), .Result(X0X1ALU_result));  // open: ErrorBit
  thirtyTwoBitALU X1Y1ALU (
    .A(X1Y1_q[31:0]), .B(X1Y1_q[63:32]), .Opcode(Op), .shiftAmount(shiftAmount), .Result(X1Y1ALU_result));  // open: ErrorBit
  thirtyTwoBitALU Y0Y1ALU (
    .A(X0Y0_q[63:32]), .B(X1Y1_q[63:32]), .Opcode(Op), .shiftAmount(shiftAmount), .Result(Y0Y1ALU_result));  // open: ErrorBit
  Register #(.width(32)) register_1 (
    .D(X0Y0ALU_result), .clk(clock_1_out), .Q(out_8), .clr(ClearRegisters));  // open: en
  Register #(.width(32)) register_2 (
    .D(X0X1ALU_result), .clk(clock_1_out), .Q(out_9), .clr(ClearRegisters));  // open: en
  Register #(.width(32)) register_3 (
    .D(X1Y1ALU_result), .clk(clock_1_out), .Q(out_10), .clr(ClearRegisters));  // open: en
  Register #(.width(32)) register_4 (
    .D(Y0Y1ALU_result), .clk(clock_1_out), .Q(out_11), .clr(ClearRegisters));  // open: en
endmodule

module thirtyTwoBitALU (
  input  [31:0] A,
  input  [31:0] B,
  input  [3:0] Opcode,
  input  [4:0] shiftAmount,
  output [31:0] Result,
  output ErrorBit
);

  wire arithmeticwithshiftlogic_1_overflowflag, equivalenceslogic_1_result, not_1_out;
  wire [31:0] arithmeticwithshiftlogic_1_result, bit_extender_1_out, directopslogic_1_result,
       multiplexer_1_out;

  // Probe on B
  // Probe on A
  directOpsLogic directopslogic_1 (.A(A), .B(B), .shiftAmount(Opcode[2:1]), .Result(directopslogic_1_result));
  ArithmeticWithShiftLogic arithmeticwithshiftlogic_1 (
    .Cin(Opcode[1]), .B(B), .A(A), .shiftAmount(shiftAmount), .OpIn(Opcode[2:0]),
    .Result(arithmeticwithshiftlogic_1_result), .Overflowflag(arithmeticwithshiftlogic_1_overflowflag));
  EquivalencesLogic equivalenceslogic_1 (.A(A), .B(B), .OpIn(Opcode[2:1]), .Result(equivalenceslogic_1_result));
  assign bit_extender_1_out = {{31{1'b0}}, equivalenceslogic_1_result};  // Bit_Extender bit_extender_1
  not not_1 (not_1_out, Opcode[3]);
  and and_1 (ErrorBit, arithmeticwithshiftlogic_1_overflowflag, not_1_out);
  Multiplexer #(.enable("false"), .width(32)) multiplexer_1 (
    .in0(directopslogic_1_result), .in1(bit_extender_1_out), .out(multiplexer_1_out), .sel(Opcode[0]));
  Multiplexer #(.enable("false"), .width(32)) multiplexer_2 (
    .in0(arithmeticwithshiftlogic_1_result), .in1(multiplexer_1_out), .out(Result), .sel(Opcode[3]));
  // Probe on bit_extender_1_out
endmodule

module IntMul (
  input  [31:0] Ain,
  input  [31:0] Bin,
  output [31:0] result,
  output Overflow
);

  wire [31:0] multiplier_1_cout;

  // Probe on multiplier_1_cout
  Multiplier #(.mode("twosComplement"), .width(32)) multiplier_1 (
    .a(Ain), .b(Bin), .out(result), .cout(multiplier_1_cout));  // open: cin
  or or_1 (Overflow, multiplier_1_cout[31], multiplier_1_cout[30], multiplier_1_cout[29], multiplier_1_cout[28], multiplier_1_cout[27], multiplier_1_cout[26], multiplier_1_cout[25], multiplier_1_cout[24], multiplier_1_cout[23], multiplier_1_cout[22], multiplier_1_cout[21], multiplier_1_cout[20], multiplier_1_cout[19], multiplier_1_cout[18], multiplier_1_cout[17], multiplier_1_cout[16], multiplier_1_cout[15], multiplier_1_cout[14], multiplier_1_cout[13], multiplier_1_cout[12], multiplier_1_cout[11], multiplier_1_cout[10], multiplier_1_cout[9], multiplier_1_cout[8], multiplier_1_cout[7], multiplier_1_cout[6], multiplier_1_cout[5], multiplier_1_cout[4], multiplier_1_cout[3], multiplier_1_cout[2], multiplier_1_cout[1], multiplier_1_cout[0]);
endmodule
