// Logisim project FPUMul.circ as structural Verilog: 4 circuits, main circuit FPUMulStage1
module FPUMulStage1 (
  input  [31:0] Ain,
  input  [31:0] Bin,
  output [31:0] Aout,
  output SignOut,
  output [31:0] Bout
);

  xor xor_1 (SignOut, Ain[31], Bin[31]);

  assign Aout = Ain;
  assign Bout = Bin;
endmodule

module FPUMulStage2 (
  input  [31:0] Ain,
  input  [31:0] Bin,
  input  SignIn,
  output [31:0] Aout,
  output [7:0] ExponentOut,
  output [31:0] Bout,
  output SignOut
);

  wire adder_1_cout;
  wire [7:0] adder_1_out;

  Adder adder_1 (.a(Ain[30:23]), .b(Bin[30:23]), .out(adder_1_out), .cout(adder_1_cout));  // open: cin
  Subtractor subtractor_1 (.a(adder_1_out), .b(8'h7f), .out(ExponentOut));  // open: bin, bout

  assign Aout = Ain;
  assign Bout = Bin;
  assign SignOut = SignIn;
endmodule

module FPUMulStage3 (
  input  [31:0] Ain,
  input  [31:0] Bin,
  input  [7:0] ExponentIn,
  input  SignIn,
  output [31:0] FPUMulResult,
  output Overflow
);

  wire and_1_out, nor_1_out, nor_2_out, or_1_out;
  wire [7:0] adder_1_out;
  wire [22:0] multiplexer_1_out, multiplier_1_out, multiplier_1_out_2;
  wire [23:22] multiplier_1_cout;
  wire [31:0] multiplexer_2_out;

  nor nor_1 (nor_1_out, 1'b0, Bin[30], Bin[29], Bin[28], Bin[27], Bin[26], Bin[25], Bin[24], Bin[23], Bin[22], Bin[21], Bin[20], Bin[19], Bin[18], Bin[17], Bin[16], Bin[15], Bin[14], Bin[13], Bin[12], Bin[11], Bin[10], Bin[9], Bin[8], Bin[7], Bin[6], Bin[5], Bin[4], Bin[3], Bin[2], Bin[1], Bin[0]);
  Multiplier #(.width(24)) multiplier_1 (
    .a({1'b1, Ain[22:0]}), .b({1'b1, Bin[22:0]}), .out({multiplier_1_out_2[0], multiplier_1_out}),
    .cout({multiplier_1_cout, multiplier_1_out_2[22:1]}));  // open: cin
  // Probe on multiplier_1_out_2[22:1]
  Adder adder_1 (.a(ExponentIn), .b({8{1'b0}}), .out(adder_1_out), .cin(multiplier_1_cout[23]), .cout(Overflow));
  // Probe on multiplier_1_out_2
  Multiplexer #(.enable("false"), .width(23)) multiplexer_1 (
    .in0(multiplier_1_out_2), .in1({multiplier_1_cout[22], multiplier_1_out_2[22:1]}),
    .out(multiplexer_1_out), .sel(multiplier_1_cout[23]));
  nor nor_2 (nor_2_out, 1'b0, Ain[30], Ain[29], Ain[28], Ain[27], Ain[26], Ain[25], Ain[24], Ain[23], Ain[22], Ain[21], Ain[20], Ain[19], Ain[18], Ain[17], Ain[16], Ain[15], Ain[14], Ain[13], Ain[12], Ain[11], Ain[10], Ain[9], Ain[8], Ain[7], Ain[6], Ain[5], Ain[4], Ain[3], Ain[2], Ain[1], Ain[0]);
  or or_1 (or_1_out, nor_2_out, nor_1_out);
  // Probe on {SignIn, adder_1_out, multiplexer_1_out}
  Multiplexer #(.enable("false"), .width(32)) multiplexer_2 (
    .in0({SignIn, adder_1_out, multiplexer_1_out}), .in1({32{1'b0}}), .out(multiplexer_2_out), .sel(or_1_out));
  Multiplexer #(.enable("false"), .width(32)) multiplexer_3 (
    .in0(multiplexer_2_out), .in1(32'h80000000), .out(FPUMulResult), .sel(and_1_out));
  and and_1 (and_1_out, or_1_out, SignIn);
endmodule

module FPUMul (
  input  [31:0] Ain,
  input  [31:0] Bin,
  output [31:0] FPUMulResult,
  output Overflow
);

  wire fpumulstage1_1_signout, fpumulstage2_1_signout, undriven;
  wire [7:0] fpumulstage2_1_exponentout;
  wire [31:0] fpumulstage1_1_aout, fpumulstage1_1_bout, fpumulstage2_1_aout, fpumulstage2_1_bout;

  FPUMulStage1 fpumulstage1_1 (
    .Ain(Ain), .Bin(Bin), .Aout(fpumulstage1_1_aout), .SignOut(fpumulstage1_1_signout),
    .Bout(fpumulstage1_1_bout));
  // Probe on undriven
  FPUMulStage2 fpumulstage2_1 (
    .Ain(fpumulstage1_1_aout), .Bin(fpumulstage1_1_bout), .SignIn(fpumulstage1_1_signout),
    .Aout(fpumulstage2_1_aout), .ExponentOut(fpumulstage2_1_exponentout), .Bout(fpumulstage2_1_bout),
    .SignOut(fpumulstage2_1_signout));
  FPUMulStage3 fpumulstage3_1 (
    .Ain(fpumulstage2_1_aout), .Bin(fpumulstage2_1_bout), .ExponentIn(fpumulstage2_1_exponentout),
    .SignIn(fpumulstage2_1_signout), .FPUMulResult(FPUMulResult), .Overflow(Overflow));
endmodule
