// Logisim project FPUadder32Bit.circ as structural Verilog: 9 circuits, main circuit subReduce1
module subReduce1 (
  input  [23:0] realSub1A,
  output [23:0] realSub1B,
  output realSub1Out
);

  wire [4:4] pull_resistor_1_node;

  not not_1 (realSub1Out, realSub1A[23]);
  Pull_Resistor pull_resistor_1 (.node(pull_resistor_1_node[4]));
  Shifter #(.width(24)) shifter_1 (
    .in(realSub1A), .\dist ({{4{pull_resistor_1_node[4]}}, realSub1Out}), .out(realSub1B));
endmodule

module subReduce2 (
  input  [23:0] realSub2A,
  output [23:0] realSub2B,
  output realSub2Out
);

  wire bitfinder_1_found;
  wire [4:4] pull_resistor_1_node;

  BitFinder #(.width(2)) bitfinder_1 (.in(realSub2A[23:22]), .found(bitfinder_1_found));  // open: index
  not not_1 (realSub2Out, bitfinder_1_found);
  Pull_Resistor pull_resistor_1 (.node(pull_resistor_1_node[4]));
  Shifter #(.width(24)) shifter_1 (
    .in(realSub2A), .\dist ({{4{pull_resistor_1_node[4]}}, realSub2Out}), .out(realSub2B));
endmodule

module subReduce4 (
  input  [23:0] realSub4A,
  output [23:0] realSub4B,
  output realSub4Out
);

  wire bitfinder_1_found;
  wire [4:4] pull_resistor_1_node;

  BitFinder #(.width(4)) bitfinder_1 (.in(realSub4A[23:20]), .found(bitfinder_1_found));  // open: index
  not not_1 (realSub4Out, bitfinder_1_found);
  Pull_Resistor pull_resistor_1 (.node(pull_resistor_1_node[4]));
  Shifter #(.width(24)) shifter_1 (
    .in(realSub4A), .\dist ({{4{pull_resistor_1_node[4]}}, realSub4Out}), .out(realSub4B));
endmodule

module subReduce8 (
  input  [23:0] realSub8A,
  output [23:0] realSub8B,
  output realSub8Out
);

  wire bitfinder_1_found;
  wire [4:4] pull_resistor_1_node;

  BitFinder bitfinder_1 (.in(realSub8A[23:16]), .found(bitfinder_1_found));  // open: index
  not not_1 (realSub8Out, bitfinder_1_found);
  Pull_Resistor pull_resistor_1 (.node(pull_resistor_1_node[4]));
  Shifter #(.width(24)) shifter_1 (
    .in(realSub8A), .\dist ({{4{pull_resistor_1_node[4]}}, realSub8Out}), .out(realSub8B));
endmodule

module subReduce16 (
  input  [23:0] realSub16A,
  output realSub16Out,
  output [23:0] realSub16B
);

  wire bitfinder_1_found;

  Multiplexer #(.enable("false"), .width(8)) multiplexer_1 (
    .in0(realSub16A[7:0]), .in1(realSub16A[23:16]), .out(realSub16B[23:16]), .sel(bitfinder_1_found));
  Multiplexer #(.enable("false"), .width(8)) multiplexer_2 (
    .in0({8{1'b0}}), .in1(realSub16A[15:8]), .out(realSub16B[15:8]), .sel(bitfinder_1_found));
  Multiplexer #(.enable("false"), .width(8)) multiplexer_3 (
    .in0({8{1'b0}}), .in1(realSub16A[7:0]), .out(realSub16B[7:0]), .sel(bitfinder_1_found));
  BitFinder #(.width(16)) bitfinder_1 (.in(realSub16A[23:8]), .found(bitfinder_1_found));  // open: index
  not not_1 (realSub16Out, bitfinder_1_found);
endmodule

module normalize (
  input  [23:0] subReduceA,
  output realSub16Out,
  output [23:0] subReduceB,
  output realSub8Out,
  output realSub4Out,
  output realSub2Out,
  output realSub1Out
);

  wire [23:0] subreduce1_1_realsub1b, subreduce2_1_realsub2b, subreduce4_1_realsub4b, subreduce8_1_realsub8b;

  subReduce16 subreduce16_1 (.realSub16A(subreduce8_1_realsub8b), .realSub16Out(realSub16Out), .realSub16B(subReduceB));
  subReduce8 subreduce8_1 (
    .realSub8A(subreduce4_1_realsub4b), .realSub8B(subreduce8_1_realsub8b), .realSub8Out(realSub8Out));
  subReduce4 subreduce4_1 (
    .realSub4A(subreduce2_1_realsub2b), .realSub4B(subreduce4_1_realsub4b), .realSub4Out(realSub4Out));
  subReduce2 subreduce2_1 (
    .realSub2A(subreduce1_1_realsub1b), .realSub2B(subreduce2_1_realsub2b), .realSub2Out(realSub2Out));
  subReduce1 subreduce1_1 (.realSub1A(subReduceA), .realSub1B(subreduce1_1_realsub1b), .realSub1Out(realSub1Out));
endmodule

module realOpCheck (
  input  SubMode,
  input  ASign,
  input  BSign,
  output Sub,
  output Switch
);

  wire xor_1_out;

  xor xor_1 (xor_1_out, ASign, BSign);
  xor xor_2 (Sub, SubMode, xor_1_out);
  and and_1 (Switch, ASign, ~BSign, ~SubMode);  // AND_Gate
endmodule

module FPUAdder (
  input  FloatSubMode,
  input  [31:0] Float32A,
  input  [31:0] Float32B,
  output [31:0] FloatResult
);

  wire adder_1_cout, bitfinder_1_found, realopcheck_1_sub, realopcheck_1_switch, subtractor_3_bout, undriven,
       zerohandler_1_out_3;
  wire [4:0] and_1_out, normalize_1_realsub1out;
  wire [7:0] adder_2_out, and_2_out, multiplexer_3_out, or_1_out, subtractor_1_out, subtractor_2_out;
  wire [7:5] and_1_out_2;
  wire [7:7] adder_2_cout, subtractor_1_bout, subtractor_2_bout;
  wire [22:0] adder_1_out, and_3_out, multiplexer_1_out_2, multiplexer_5_out;
  wire [22:22] adder_1_out_2;
  wire [23:0] multiplexer_4_out, normalize_1_subreduceb, shifter_1_out, shifter_2_out, subtractor_3_out,
       subtractor_4_out;
  wire [30:23] multiplexer_1_out;
  wire [31:0] multiplexer_2_out, multiplexer_6_out, multiplexer_7_out, or_3_out;
  wire [31:23] subtractor_5_out;
  wire [31:31] multiplexer_1_out_3;

  Multiplexer #(.enable("false"), .width(32)) multiplexer_1 (
    .in0(Float32A), .in1(Float32B), .out({multiplexer_1_out_3[31], multiplexer_1_out, multiplexer_1_out_2}),
    .sel(realopcheck_1_switch));
  Multiplexer #(.enable("false"), .width(32)) multiplexer_2 (
    .in0(Float32B), .in1(Float32A), .out(multiplexer_2_out), .sel(realopcheck_1_switch));
  realOpCheck realopcheck_1 (
    .SubMode(FloatSubMode), .ASign(Float32A[31]), .BSign(Float32B[31]), .Sub(realopcheck_1_sub),
    .Switch(realopcheck_1_switch));
  ZeroHandler zerohandler_1 (.Ain(Float32A), .Bin(Float32B), .out_3(zerohandler_1_out_3));
  Subtractor subtractor_1 (
    .a(multiplexer_2_out[30:23]), .b(multiplexer_1_out), .out(subtractor_1_out), .bout(subtractor_1_bout[7]));  // open: bin
  Subtractor subtractor_2 (
    .a(multiplexer_1_out), .b(multiplexer_2_out[30:23]), .out(subtractor_2_out), .bout(subtractor_2_bout[7]));  // open: bin
  Multiplexer #(.enable("false"), .width(8)) multiplexer_3 (
    .in0(multiplexer_1_out), .in1(multiplexer_2_out[30:23]), .out(multiplexer_3_out),
    .sel(subtractor_2_bout[7]));
  assign {and_1_out_2, and_1_out} = subtractor_2_out & ~{8{subtractor_2_bout[7]}};  // AND_Gate and_1, 8 bits wide
  Shifter #(.shift("lr"), .width(24)) shifter_1 (
    .in({1'b1, multiplexer_2_out[22:0]}), .\dist (and_1_out), .out(shifter_1_out));
  assign and_2_out = subtractor_1_out & ~{8{subtractor_1_bout[7]}};  // AND_Gate and_2, 8 bits wide
  Shifter #(.shift("lr"), .width(24)) shifter_2 (
    .in({1'b1, multiplexer_1_out_2}), .\dist (and_2_out[4:0]), .out(shifter_2_out));
  Adder #(.width(24)) adder_1 (
    .a(shifter_2_out), .b(shifter_1_out), .out({adder_1_out_2[22], adder_1_out}), .cout(adder_1_cout));  // open: cin
  Subtractor #(.width(24)) subtractor_3 (
    .a(shifter_2_out), .b(shifter_1_out), .out(subtractor_3_out), .bout(subtractor_3_bout));  // open: bin
  Subtractor #(.width(24)) subtractor_4 (
    .a(shifter_1_out), .b(shifter_2_out), .out(subtractor_4_out));  // open: bin, bout
  Multiplexer #(.enable("false"), .width(24)) multiplexer_4 (
    .in0(subtractor_3_out), .in1(subtractor_4_out), .out(multiplexer_4_out), .sel(subtractor_3_bout));
  Multiplexer #(.enable("false"), .width(23)) multiplexer_5 (
    .in0(adder_1_out), .in1({adder_1_out_2[22], adder_1_out[22:1]}), .out(multiplexer_5_out),
    .sel(adder_1_cout));
  Adder adder_2 (.a({8{1'b0}}), .b(multiplexer_3_out), .out(adder_2_out), .cin(adder_1_cout), .cout(adder_2_cout[7]));
  BitFinder #(.width(24)) bitfinder_1 (.in(multiplexer_4_out), .found(bitfinder_1_found));  // open: index
  normalize normalize_1 (
    .subReduceA(multiplexer_4_out), .realSub16Out(normalize_1_realsub1out[4]),
    .subReduceB(normalize_1_subreduceb), .realSub8Out(normalize_1_realsub1out[3]),
    .realSub4Out(normalize_1_realsub1out[2]), .realSub2Out(normalize_1_realsub1out[1]),
    .realSub1Out(normalize_1_realsub1out[0]));
  assign or_1_out = {8{adder_2_cout[7]}} | adder_2_out;  // OR_Gate or_1, 8 bits wide
  assign and_3_out = multiplexer_5_out & ~{23{adder_2_cout[7]}};  // AND_Gate and_3, 23 bits wide
  Multiplexer #(.enable("false"), .width(32)) multiplexer_6 (
    .in0({32{1'b0}}), .in1({subtractor_5_out, normalize_1_subreduceb[22:0]}), .out(multiplexer_6_out),
    .sel(bitfinder_1_found));
  Subtractor subtractor_5 (
    .a(multiplexer_3_out), .b({3'b000, normalize_1_realsub1out}), .out(subtractor_5_out[30:23]));  // open: bin, bout
  or or_2 (subtractor_5_out[31], subtractor_3_bout, multiplexer_1_out_3[31]);
  // Probe on multiplexer_7_out
  Multiplexer #(.enable("false"), .width(32)) multiplexer_7 (
    .in0({multiplexer_1_out_3[31], or_1_out, and_3_out}), .in1(multiplexer_6_out), .out(multiplexer_7_out),
    .sel(realopcheck_1_sub));
  assign or_3_out = Float32A | Float32B;  // OR_Gate or_3, 32 bits wide
  Multiplexer #(.enable("false"), .width(32)) multiplexer_8 (
    .in0(multiplexer_7_out), .in1(or_3_out), .out(FloatResult), .sel(zerohandler_1_out_3));
  // Probe on undriven
endmodule

module ZeroHandler (
  input  [31:0] Ain,
  input  [31:0] Bin,
  output out_3
);

  wire nor_1_out, nor_2_out, nor_3_out, nor_4_out, or_1_out;

  nor nor_1 (nor_1_out, Ain[0], Ain[1], Ain[2], Ain[3], Ain[4], Ain[5], Ain[6], Ain[7], Ain[8], Ain[9], Ain[10], Ain[11], Ain[12], Ain[13], Ain[14], Ain[15], Ain[16], Ain[17], Ain[18], Ain[19], Ain[20], Ain[21], Ain[22], Ain[23], Ain[24], Ain[25], Ain[26], Ain[27], Ain[28], Ain[29], Ain[30], Ain[31]);
  nor nor_2 (nor_2_out, Bin[0], Bin[1], Bin[2], Bin[3], Bin[4], Bin[5], Bin[6], Bin[7], Bin[8], Bin[9], Bin[10], Bin[11], Bin[12], Bin[13], Bin[14], Bin[15], Bin[16], Bin[17], Bin[18], Bin[19], Bin[20], Bin[21], Bin[22], Bin[23], Bin[24], Bin[25], Bin[26], Bin[27], Bin[28], Bin[29], Bin[30], Bin[31]);
  nor nor_3 (nor_3_out, Ain[0], Ain[1], Ain[2], Ain[3], Ain[4], Ain[5], Ain[6], Ain[7], Ain[8], Ain[9], Ain[10], Ain[11], Ain[12], Ain[13], Ain[14], Ain[15], Ain[16], Ain[17], Ain[18], Ain[19], Ain[20], Ain[21], Ain[22], Ain[23], Ain[24], Ain[25], Ain[26], Ain[27], Ain[28], Ain[29], Ain[30], 1'b0);
  nor nor_4 (nor_4_out, Bin[0], Bin[1], Bin[2], Bin[3], Bin[4], Bin[5], Bin[6], Bin[7], Bin[8], Bin[9], Bin[10], Bin[11], Bin[12], Bin[13], Bin[14], Bin[15], Bin[16], Bin[17], Bin[18], Bin[19], Bin[20], Bin[21], Bin[22], Bin[23], Bin[24], Bin[25], Bin[26], Bin[27], Bin[28], Bin[29], Bin[30], 1'b0);
  or or_1 (or_1_out, nor_1_out, nor_2_out);
  or or_2 (out_3, nor_3_out, nor_4_out);
endmodule
