// Logisim project LogismShaderCore.circ as structural Verilog: 3 circuits, main circuit ShaderCore
module ShaderCore (
  output [31:0] out_1,
  output [31:0] out_2,
  output [31:0] out_3,
  output [31:0] out_4
);

  wire undriven_3;
  wire [4:0] undriven;
  wire [5:0] undriven_2;
  wire [31:0] registerfile_1_readdata1out, registerfile_1_readdata2out, registerfile_1_readdata3out,
       registerfile_1_readdata4out;

  RegisterFile registerfile_1 (
    .ReadData1Out(registerfile_1_readdata1out), .ReadData2Out(registerfile_1_readdata2out),
    .ReadData3Out(registerfile_1_readdata3out), .ReadData4Out(registerfile_1_readdata4out));  // open: WriteDataIn, WriteRegInBlock1, WriteRegInBlock2, ReadDataIn1, ReadDataIn2, ReadDataIn3, ReadDataIn4, regWrite
  SimdShader simdshader_1 (
    .X0(registerfile_1_readdata1out), .Y0(registerfile_1_readdata2out), .X1(registerfile_1_readdata3out),
    .Y1(registerfile_1_readdata4out), .shiftIn(undriven), .Op(undriven_2), .ClearRegisters(undriven_3),
    .out_8(out_1), .out_9(out_2), .out_10(out_3), .out_11(out_4));
endmodule

module ShaderExecuteBackend (
  input  [31:0] Ain,
  input  [31:0] Bin,
  input  [5:0] OpCode,
  input  [4:0] ShiftIn,
  output [31:0] out_5
);

  wire [31:0] fpuadder_1_floatresult, fpumul_1_fpumulresult, thirtytwobitalu_1_result;

  thirtyTwoBitALU thirtytwobitalu_1 (
    .A(Ain), .B(Bin), .Opcode(OpCode[3:0]), .shiftAmount(ShiftIn), .Result(thirtytwobitalu_1_result));  // open: ErrorBit
  FPUMul fpumul_1 (.Ain(Ain), .Bin(Bin), .FPUMulResult(fpumul_1_fpumulresult));
  FPUAdder fpuadder_1 (.FloatSubMode(OpCode[0]), .Float32A(Ain), .Float32B(Bin), .FloatResult(fpuadder_1_floatresult));
  // Probe on thirtytwobitalu_1_result
  // Probe on out_5
  Multiplexer #(.enable("false"), .select(2), .width(32)) multiplexer_1 (
    .in0(thirtytwobitalu_1_result), .in1(thirtytwobitalu_1_result), .in2(fpumul_1_fpumulresult),
    .in3(fpuadder_1_floatresult), .out(out_5), .sel({OpCode[4], OpCode[5]}));
  // Probe on fpuadder_1_floatresult
  // Probe on out_5
endmodule

module SimdShader (
  input  [31:0] X0,
  input  [31:0] Y0,
  input  [31:0] X1,
  input  [31:0] Y1,
  input  [4:0] shiftIn,
  input  [5:0] Op,
  input  ClearRegisters,
  output [31:0] out_8,
  output [31:0] out_9,
  output [31:0] out_10,
  output [31:0] out_11
);

  wire ClockIn_out;
  wire [31:0] X0X1Shader_out_5, X0Y0Shader_out_5, X1Y1Shader_out_5, Y1Y0Shader_out_5;
  wire [63:0] X0Y0_q, X1Y1_q;

  Clock ClockIn (.out(ClockIn_out));
  Register #(.width(64)) X0Y0 (.D({Y0, X0}), .clk(ClockIn_out), .Q(X0Y0_q), .clr(ClearRegisters));  // open: en
  Register #(.width(64)) X1Y1 (.D({Y1, X1}), .clk(ClockIn_out), .Q(X1Y1_q), .clr(ClearRegisters));  // open: en
  ShaderExecuteBackend X0Y0Shader (
    .Ain(X0Y0_q[31:0]), .Bin(X0Y0_q[63:32]), .OpCode(Op), .ShiftIn(shiftIn), .out_5(X0Y0Shader_out_5));
  ShaderExecuteBackend X0X1Shader (
    .Ain(X0Y0_q[31:0]), .Bin(X1Y1_q[31:0]), .OpCode(Op), .ShiftIn(shiftIn), .out_5(X0X1Shader_out_5));
  ShaderExecuteBackend X1Y1Shader (
    .Ain(X1Y1_q[31:0]), .Bin(X1Y1_q[63:32]), .OpCode(Op), .ShiftIn(shiftIn), .out_5(X1Y1Shader_out_5));
  ShaderExecuteBackend Y1Y0Shader (
    .Ain(X0Y0_q[63:32]), .Bin(X1Y1_q[63:32]), .OpCode(Op), .ShiftIn(shiftIn), .out_5(Y1Y0Shader_out_5));
  Register #(.width(32)) register_1 (
    .D(X0Y0Shader_out_5), .clk(ClockIn_out), .Q(out_8), .clr(ClearRegisters));  // open: en
  Register #(.width(32)) register_2 (
    .D(X0X1Shader_out_5), .clk(ClockIn_out), .Q(out_9), .clr(ClearRegisters));  // open: en
  Register #(.width(32)) register_3 (
    .D(X1Y1Shader_out_5), .clk(ClockIn_out), .Q(out_10), .clr(ClearRegisters));  // open: en
  Register #(.width(32)) register_4 (
    .D(Y1Y0Shader_out_5), .clk(ClockIn_out), .Q(out_11), .clr(ClearRegisters));  // open: en
endmodule
