// Logisim project RegisterFile.circ as structural Verilog: 1 circuit, main circuit RegisterFile
module RegisterFile (
  input  [31:0] WriteDataIn,
  input  [4:0] WriteRegInBlock1,
  input  [4:0] WriteRegInBlock2,
  input  [4:0] ReadDataIn1,
  input  [4:0] ReadDataIn2,
  input  [4:0] ReadDataIn3,
  input  [4:0] ReadDataIn4,
  input  regWrite,
  output [31:0] ReadData1Out,
  output [31:0] ReadData2Out,
  output [31:0] ReadData3Out,
  output [31:0] ReadData4Out
);

  wire and_1_out, and_2_out, and_3_out, and_4_out, and_5_out, and_6_out, and_7_out, and_8_out, and_9_out,
       and_10_out, and_11_out, and_12_out, and_13_out, and_14_out, and_15_out, and_16_out, and_17_out,
       and_18_out, and_19_out, and_20_out, and_21_out, and_22_out, and_23_out, and_24_out, and_25_out,
       and_26_out, and_27_out, and_28_out, and_29_out, and_30_out, and_31_out, and_32_out, and_33_out,
       and_34_out, and_35_out, and_36_out, and_37_out, and_38_out, and_39_out, and_40_out, and_41_out,
       and_42_out, and_43_out, and_44_out, and_45_out, and_46_out, and_47_out, and_48_out, and_49_out,
       and_50_out, and_51_out, and_52_out, and_53_out, and_54_out, and_55_out, and_56_out, and_57_out,
       and_58_out, and_59_out, and_60_out, and_61_out, and_62_out, and_63_out, and_64_out, ClockIn_out,
       undriven, undriven_2, undriven_3, undriven_4, undriven_5, undriven_6, undriven_7, undriven_8;
  wire [31:0] register_1_q, register_2_q, register_3_q, register_4_q, register_5_q, register_6_q,
       register_7_q, register_8_q, register_9_q, register_10_q, register_11_q, register_12_q, register_13_q,
       register_14_q, register_15_q, register_16_q, register_17_q, register_18_q, register_19_q,
       register_20_q, register_21_q, register_22_q, register_23_q, register_24_q, register_25_q,
       register_26_q, register_27_q, register_28_q, register_29_q, register_30_q, register_31_q,
       register_32_q, register_33_q, register_34_q, register_35_q, register_36_q, register_37_q,
       register_38_q, register_39_q, register_40_q, register_41_q, register_42_q, register_43_q,
       register_44_q, register_45_q, register_46_q, register_47_q, register_48_q, register_49_q,
       register_50_q, register_51_q, register_52_q, register_53_q, register_54_q, register_55_q,
       register_56_q, register_57_q, register_58_q, register_59_q, register_60_q, register_61_q,
       register_62_q, register_63_q, register_64_q;
  wire [63:0] decoder_1_out0;

  Clock ClockIn (.out(ClockIn_out));
  Decoder #(.select(5)) decoder_1 (
    .out0(decoder_1_out0[0]), .out1(decoder_1_out0[1]), .out2(decoder_1_out0[2]), .out3(decoder_1_out0[3]),
    .out4(decoder_1_out0[4]), .out5(decoder_1_out0[5]), .out6(decoder_1_out0[6]), .out7(decoder_1_out0[7]),
    .out8(decoder_1_out0[8]), .out9(decoder_1_out0[9]), .out10(decoder_1_out0[10]),
    .out11(decoder_1_out0[11]), .out12(decoder_1_out0[12]), .out13(decoder_1_out0[13]),
    .out14(decoder_1_out0[14]), .out15(decoder_1_out0[15]), .out16(decoder_1_out0[16]),
    .out17(decoder_1_out0[17]), .out18(decoder_1_out0[18]), .out19(decoder_1_out0[19]),
    .out20(decoder_1_out0[20]), .out21(decoder_1_out0[21]), .out22(decoder_1_out0[22]),
    .out23(decoder_1_out0[23]), .out24(decoder_1_out0[24]), .out25(decoder_1_out0[25]),
    .out26(decoder_1_out0[26]), .out27(decoder_1_out0[27]), .out28(decoder_1_out0[28]),
    .out29(decoder_1_out0[29]), .out30(decoder_1_out0[30]), .out31(decoder_1_out0[31]), .sel(WriteRegInBlock1));  // open: en
  Decoder #(.select(5)) decoder_2 (
    .out0(decoder_1_out0[32]), .out1(decoder_1_out0[33]), .out2(decoder_1_out0[34]),
    .out3(decoder_1_out0[35]), .out4(decoder_1_out0[36]), .out5(decoder_1_out0[37]),
    .out6(decoder_1_out0[38]), .out7(decoder_1_out0[39]), .out8(decoder_1_out0[40]),
    .out9(decoder_1_out0[41]), .out10(decoder_1_out0[42]), .out11(decoder_1_out0[43]),
    .out12(decoder_1_out0[44]), .out13(decoder_1_out0[45]), .out14(decoder_1_out0[46]),
    .out15(decoder_1_out0[47]), .out16(decoder_1_out0[48]), .out17(decoder_1_out0[49]),
    .out18(decoder_1_out0[50]), .out19(decoder_1_out0[51]), .out20(decoder_1_out0[52]),
    .out21(decoder_1_out0[53]), .out22(decoder_1_out0[54]), .out23(decoder_1_out0[55]),
    .out24(decoder_1_out0[56]), .out25(decoder_1_out0[57]), .out26(decoder_1_out0[58]),
    .out27(decoder_1_out0[59]), .out28(decoder_1_out0[60]), .out29(decoder_1_out0[61]),
    .out30(decoder_1_out0[62]), .out31(decoder_1_out0[63]), .sel(WriteRegInBlock2));  // open: en
  and and_1 (and_1_out, decoder_1_out0[0], regWrite);
  and and_2 (and_2_out, decoder_1_out0[1], regWrite);
  and and_3 (and_3_out, decoder_1_out0[2], regWrite);
  and and_4 (and_4_out, decoder_1_out0[3], regWrite);
  and and_5 (and_5_out, decoder_1_out0[4], regWrite);
  and and_6 (and_6_out, decoder_1_out0[5], regWrite);
  and and_7 (and_7_out, decoder_1_out0[6], regWrite);
  and and_8 (and_8_out, decoder_1_out0[7], regWrite);
  Register #(.width(32)) register_1 (
    .D(WriteDataIn), .clk(ClockIn_out), .Q(register_1_q), .clr(and_1_out));  // open: en
  Register #(.width(32)) register_2 (
    .D(WriteDataIn), .clk(ClockIn_out), .Q(register_2_q), .clr(and_2_out));  // open: en
  Register #(.width(32)) register_3 (
    .D(WriteDataIn), .clk(ClockIn_out), .Q(register_3_q), .clr(and_3_out));  // open: en
  Register #(.width(32)) register_4 (
    .D(WriteDataIn), .clk(ClockIn_out), .Q(register_4_q), .clr(and_4_out));  // open: en
  Register #(.width(32)) register_5 (
    .D(WriteDataIn), .clk(ClockIn_out), .Q(register_5_q), .clr(and_5_out));  // open: en
  Register #(.width(32)) register_6 (
    .D(WriteDataIn), .en(undriven), .clk(ClockIn_out), .Q(register_6_q), .clr(and_6_out));
  Register #(.width(32)) register_7 (
    .D(WriteDataIn), .clk(ClockIn_out), .Q(register_7_q), .clr(and_7_out));  // open: en
  Register #(.width(32)) register_8 (
    .D(WriteDataIn), .clk(ClockIn_out), .Q(register_8_q), .clr(and_8_out));  // open: en
  // Probe on register_3_q
  and and_9 (and_9_out, decoder_1_out0[8], regWrite);
  and and_10 (and_10_out, decoder_1_out0[9], regWrite);
  and and_11 (and_11_out, decoder_1_out0[10], regWrite);
  and and_12 (and_12_out, decoder_1_out0[11], regWrite);
  and and_13 (and_13_out, decoder_1_out0[12], regWrite);
  and and_14 (and_14_out, decoder_1_out0[13], regWrite);
  and and_15 (and_15_out, decoder_1_out0[14], regWrite);
  and and_16 (and_16_out, decoder_1_out0[15], regWrite);
  Register #(.width(32)) register_9 (
    .D(WriteDataIn), .clk(ClockIn_out), .Q(register_9_q), .clr(and_9_out));  // open: en
  Register #(.width(32)) register_10 (
    .D(WriteDataIn), .clk(ClockIn_out), .Q(register_10_q), .clr(and_10_out));  // open: en
  Register #(.width(32)) register_11 (
    .D(WriteDataIn), .clk(ClockIn_out), .Q(register_11_q), .clr(and_11_out));  // open: en
  Register #(.width(32)) register_12 (
    .D(WriteDataIn), .clk(ClockIn_out), .Q(register_12_q), .clr(and_12_out));  // open: en
  Register #(.width(32)) register_13 (
    .D(WriteDataIn), .clk(ClockIn_out), .Q(register_13_q), .clr(and_13_out));  // open: en
  Register #(.width(32)) register_14 (
    .D(WriteDataIn), .en(undriven_2), .clk(ClockIn_out), .Q(register_14_q), .clr(and_14_out));
  Register #(.width(32)) register_15 (
    .D(WriteDataIn), .clk(ClockIn_out), .Q(register_15_q), .clr(and_15_out));  // open: en
  Register #(.width(32)) register_16 (
    .D(WriteDataIn), .clk(ClockIn_out), .Q(register_16_q), .clr(and_16_out));  // open: en
  and and_17 (and_17_out, decoder_1_out0[16], regWrite);
  and and_18 (and_18_out, decoder_1_out0[17], regWrite);
  and and_19 (and_19_out, decoder_1_out0[18], regWrite);
  and and_20 (and_20_out, decoder_1_out0[19], regWrite);
  and and_21 (and_21_out, decoder_1_out0[20], regWrite);
  and and_22 (and_22_out, decoder_1_out0[21], regWrite);
  and and_23 (and_23_out, decoder_1_out0[22], regWrite);
  and and_24 (and_24_out, decoder_1_out0[23], regWrite);
  Register #(.width(32)) register_17 (
    .D(WriteDataIn), .clk(ClockIn_out), .Q(register_17_q), .clr(and_17_out));  // open: en
  Register #(.width(32)) register_18 (
    .D(WriteDataIn), .clk(ClockIn_out), .Q(register_18_q), .clr(and_18_out));  // open: en
  Register #(.width(32)) register_19 (
    .D(WriteDataIn), .clk(ClockIn_out), .Q(register_19_q), .clr(and_19_out));  // open: en
  Register #(.width(32)) register_20 (
    .D(WriteDataIn), .clk(ClockIn_out), .Q(register_20_q), .clr(and_20_out));  // open: en
  Register #(.width(32)) register_21 (
    .D(WriteDataIn), .clk(ClockIn_out), .Q(register_21_q), .clr(and_21_out));  // open: en
  Register #(.width(32)) register_22 (
    .D(WriteDataIn), .en(undriven_3), .clk(ClockIn_out), .Q(register_22_q), .clr(and_22_out));
  Register #(.width(32)) register_23 (
    .D(WriteDataIn), .clk(ClockIn_out), .Q(register_23_q), .clr(and_23_out));  // open: en
  Register #(.width(32)) register_24 (
    .D(WriteDataIn), .clk(ClockIn_out), .Q(register_24_q), .clr(and_24_out));  // open: en
  and and_25 (and_25_out, decoder_1_out0[24], regWrite);
  and and_26 (and_26_out, decoder_1_out0[25], regWrite);
  and and_27 (and_27_out, decoder_1_out0[26], regWrite);
  and and_28 (and_28_out, decoder_1_out0[27], regWrite);
  and and_29 (and_29_out, decoder_1_out0[28], regWrite);
  and and_30 (and_30_out, decoder_1_out0[29], regWrite);
  and and_31 (and_31_out, decoder_1_out0[30], regWrite);
  and and_32 (and_32_out, decoder_1_out0[31], regWrite);
  Register #(.width(32)) register_25 (
    .D(WriteDataIn), .clk(ClockIn_out), .Q(register_25_q), .clr(and_25_out));  // open: en
  Register #(.width(32)) register_26 (
    .D(WriteDataIn), .clk(ClockIn_out), .Q(register_26_q), .clr(and_26_out));  // open: en
  Register #(.width(32)) register_27 (
    .D(WriteDataIn), .clk(ClockIn_out), .Q(register_27_q), .clr(and_27_out));  // open: en
  Register #(.width(32)) register_28 (
    .D(WriteDataIn), .clk(ClockIn_out), .Q(register_28_q), .clr(and_28_out));  // open: en
  Register #(.width(32)) register_29 (
    .D(WriteDataIn), .clk(ClockIn_out), .Q(register_29_q), .clr(and_29_out));  // open: en
  Register #(.width(32)) register_30 (
    .D(WriteDataIn), .en(undriven_4), .clk(ClockIn_out), .Q(register_30_q), .clr(and_30_out));
  Register #(.width(32)) register_31 (
    .D(WriteDataIn), .clk(ClockIn_out), .Q(register_31_q), .clr(and_31_out));  // open: en
  Register #(.width(32)) register_32 (
    .D(WriteDataIn), .clk(ClockIn_out), .Q(register_32_q), .clr(and_32_out));  // open: en
  and and_33 (and_33_out, decoder_1_out0[32], regWrite);
  and and_34 (and_34_out, decoder_1_out0[33], regWrite);
  and and_35 (and_35_out, decoder_1_out0[34], regWrite);
  and and_36 (and_36_out, decoder_1_out0[35], regWrite);
  and and_37 (and_37_out, decoder_1_out0[36], regWrite);
  and and_38 (and_38_out, decoder_1_out0[37], regWrite);
  and and_39 (and_39_out, decoder_1_out0[38], regWrite);
  and and_40 (and_40_out, decoder_1_out0[39], regWrite);
  Register #(.width(32)) register_33 (
    .D(WriteDataIn), .clk(ClockIn_out), .Q(register_33_q), .clr(and_33_out));  // open: en
  Register #(.width(32)) register_34 (
    .D(WriteDataIn), .clk(ClockIn_out), .Q(register_34_q), .clr(and_34_out));  // open: en
  Register #(.width(32)) register_35 (
    .D(WriteDataIn), .clk(ClockIn_out), .Q(register_35_q), .clr(and_35_out));  // open: en
  Register #(.width(32)) register_36 (
    .D(WriteDataIn), .clk(ClockIn_out), .Q(register_36_q), .clr(and_36_out));  // open: en
  Register #(.width(32)) register_37 (
    .D(WriteDataIn), .clk(ClockIn_out), .Q(register_37_q), .clr(and_37_out));  // open: en
  Register #(.width(32)) register_38 (
    .D(WriteDataIn), .en(undriven_5), .clk(ClockIn_out), .Q(register_38_q), .clr(and_38_out));
  Register #(.width(32)) register_39 (
    .D(WriteDataIn), .clk(ClockIn_out), .Q(register_39_q), .clr(and_39_out));  // open: en
  Register #(.width(32)) register_40 (
    .D(WriteDataIn), .clk(ClockIn_out), .Q(register_40_q), .clr(and_40_out));  // open: en
  and and_41 (and_41_out, decoder_1_out0[40], regWrite);
  and and_42 (and_42_out, decoder_1_out0[41], regWrite);
  and and_43 (and_43_out, decoder_1_out0[42], regWrite);
  and and_44 (and_44_out, decoder_1_out0[43], regWrite);
  and and_45 (and_45_out, decoder_1_out0[44], regWrite);
  and and_46 (and_46_out, decoder_1_out0[45], regWrite);
  and and_47 (and_47_out, decoder_1_out0[46], regWrite);
  and and_48 (and_48_out, decoder_1_out0[47], regWrite);
  Register #(.width(32)) register_41 (
    .D(WriteDataIn), .clk(ClockIn_out), .Q(register_41_q), .clr(and_41_out));  // open: en
  Register #(.width(32)) register_42 (
    .D(WriteDataIn), .clk(ClockIn_out), .Q(register_42_q), .clr(and_42_out));  // open: en
  Register #(.width(32)) register_43 (
    .D(WriteDataIn), .clk(ClockIn_out), .Q(register_43_q), .clr(and_43_out));  // open: en
  Register #(.width(32)) register_44 (
    .D(WriteDataIn), .clk(ClockIn_out), .Q(register_44_q), .clr(and_44_out));  // open: en
  Register #(.width(32)) register_45 (
    .D(WriteDataIn), .clk(ClockIn_out), .Q(register_45_q), .clr(and_45_out));  // open: en
  Register #(.width(32)) register_46 (
    .D(WriteDataIn), .en(undriven_6), .clk(ClockIn_out), .Q(register_46_q), .clr(and_46_out));
  Register #(.width(32)) register_47 (
    .D(WriteDataIn), .clk(ClockIn_out), .Q(register_47_q), .clr(and_47_out));  // open: en
  Register #(.width(32)) register_48 (
    .D(WriteDataIn), .clk(ClockIn_out), .Q(register_48_q), .clr(and_48_out));  // open: en
  and and_49 (and_49_out, decoder_1_out0[48], regWrite);
  and and_50 (and_50_out, decoder_1_out0[49], regWrite);
  and and_51 (and_51_out, decoder_1_out0[50], regWrite);
  and and_52 (and_52_out, decoder_1_out0[51], regWrite);
  and and_53 (and_53_out, decoder_1_out0[52], regWrite);
  and and_54 (and_54_out, decoder_1_out0[53], regWrite);
  and and_55 (and_55_out, decoder_1_out0[54], regWrite);
  and and_56 (and_56_out, decoder_1_out0[55], regWrite);
  Register #(.width(32)) register_49 (
    .D(WriteDataIn), .clk(ClockIn_out), .Q(register_49_q), .clr(and_49_out));  // open: en
  Register #(.width(32)) register_50 (
    .D(WriteDataIn), .clk(ClockIn_out), .Q(register_50_q), .clr(and_50_out));  // open: en
  Register #(.width(32)) register_51 (
    .D(WriteDataIn), .clk(ClockIn_out), .Q(register_51_q), .clr(and_51_out));  // open: en
  Register #(.width(32)) register_52 (
    .D(WriteDataIn), .clk(ClockIn_out), .Q(register_52_q), .clr(and_52_out));  // open: en
  Register #(.width(32)) register_53 (
    .D(WriteDataIn), .clk(ClockIn_out), .Q(register_53_q), .clr(and_53_out));  // open: en
  Register #(.width(32)) register_54 (
    .D(WriteDataIn), .en(undriven_7), .clk(ClockIn_out), .Q(register_54_q), .clr(and_54_out));
  Register #(.width(32)) register_55 (
    .D(WriteDataIn), .clk(ClockIn_out), .Q(register_55_q), .clr(and_55_out));  // open: en
  Register #(.width(32)) register_56 (
    .D(WriteDataIn), .clk(ClockIn_out), .Q(register_56_q), .clr(and_56_out));  // open: en
  and and_57 (and_57_out, decoder_1_out0[56], regWrite);
  and and_58 (and_58_out, decoder_1_out0[57], regWrite);
  and and_59 (and_59_out, decoder_1_out0[58], regWrite);
  and and_60 (and_60_out, decoder_1_out0[59], regWrite);
  and and_61 (and_61_out, decoder_1_out0[60], regWrite);
  and and_62 (and_62_out, decoder_1_out0[61], regWrite);
  and and_63 (and_63_out, decoder_1_out0[62], regWrite);
  and and_64 (and_64_out, decoder_1_out0[63], regWrite);
  Register #(.width(32)) register_57 (
    .D(WriteDataIn), .clk(ClockIn_out), .Q(register_57_q), .clr(and_57_out));  // open: en
  Register #(.width(32)) register_58 (
    .D(WriteDataIn), .clk(ClockIn_out), .Q(register_58_q), .clr(and_58_out));  // open: en
  Register #(.width(32)) register_59 (
    .D(WriteDataIn), .clk(ClockIn_out), .Q(register_59_q), .clr(and_59_out));  // open: en
  Register #(.width(32)) register_60 (
    .D(WriteDataIn), .clk(ClockIn_out), .Q(register_60_q), .clr(and_60_out));  // open: en
  Register #(.width(32)) register_61 (
    .D(WriteDataIn), .clk(ClockIn_out), .Q(register_61_q), .clr(and_61_out));  // open: en
  Register #(.width(32)) register_62 (
    .D(WriteDataIn), .en(undriven_8), .clk(ClockIn_out), .Q(register_62_q), .clr(and_62_out));
  Register #(.width(32)) register_63 (
    .D(WriteDataIn), .clk(ClockIn_out), .Q(register_63_q), .clr(and_63_out));  // open: en
  Register #(.width(32)) register_64 (
    .D(WriteDataIn), .clk(ClockIn_out), .Q(register_64_q), .clr(and_64_out));  // open: en
  Multiplexer #(.enable("false"), .select(5), .width(32)) multiplexer_1 (
    .in0(register_1_q), .in1(register_2_q), .in2(register_3_q), .in3(register_4_q), .in4(register_5_q),
    .in5(register_6_q), .in6(register_7_q), .in7(register_8_q), .in8(register_9_q), .in9(register_10_q),
    .in10(register_11_q), .in11(register_12_q), .in12(register_13_q), .in13(register_14_q),
    .in14(register_15_q), .in15(register_16_q), .in16(register_17_q), .in17(register_18_q),
    .in18(register_19_q), .in19(register_20_q), .in20(register_21_q), .in21(register_22_q),
    .in22(register_23_q), .in23(register_24_q), .in24(register_25_q), .in25(register_26_q),
    .in26(register_27_q), .in27(register_28_q), .in28(register_29_q), .in29(register_30_q),
    .in30(register_31_q), .in31(register_32_q), .out(ReadData1Out), .sel(ReadDataIn1));
  Multiplexer #(.enable("false"), .select(5), .width(32)) multiplexer_2 (
    .in0(register_1_q), .in1(register_2_q), .in2(register_3_q), .in3(register_4_q), .in4(register_5_q),
    .in5(register_6_q), .in6(register_7_q), .in7(register_8_q), .in8(register_9_q), .in9(register_10_q),
    .in10(register_11_q), .in11(register_12_q), .in12(register_13_q), .in13(register_14_q),
    .in14(register_15_q), .in15(register_16_q), .in16(register_17_q), .in17(register_18_q),
    .in18(register_19_q), .in19(register_20_q), .in20(register_21_q), .in21(register_22_q),
    .in22(register_23_q), .in23(register_24_q), .in24(register_25_q), .in25(register_26_q),
    .in26(register_27_q), .in27(register_28_q), .in28(register_29_q), .in29(register_30_q),
    .in30(register_31_q), .in31(register_32_q), .out(ReadData3Out), .sel(ReadDataIn2));
  Multiplexer #(.enable("false"), .select(5), .width(32)) multiplexer_3 (
    .in0(register_33_q), .in1(register_34_q), .in2(register_35_q), .in3(register_36_q), .in4(register_37_q),
    .in5(register_38_q), .in6(register_39_q), .in7(register_40_q), .in8(register_41_q), .in9(register_42_q),
    .in10(register_43_q), .in11(register_44_q), .in12(register_45_q), .in13(register_46_q),
    .in14(register_47_q), .in15(register_48_q), .in16(register_49_q), .in17(register_50_q),
    .in18(register_51_q), .in19(register_52_q), .in20(register_53_q), .in21(register_54_q),
    .in22(register_55_q), .in23(register_56_q), .in24(register_57_q), .in25(register_58_q),
    .in26(register_59_q), .in27(register_60_q), .in28(register_61_q), .in29(register_62_q),
    .in30(register_63_q), .in31(register_64_q), .out(ReadData2Out), .sel(ReadDataIn3));
  Multiplexer #(.enable("false"), .select(5), .width(32)) multiplexer_4 (
    .in0(register_33_q), .in1(register_34_q), .in2(register_35_q), .in3(register_36_q), .in4(register_37_q),
    .in5(register_38_q), .in6(register_39_q), .in7(register_40_q), .in8(register_41_q), .in9(register_42_q),
    .in10(register_43_q), .in11(register_44_q), .in12(register_45_q), .in13(register_46_q),
    .in14(register_47_q), .in15(register_48_q), .in16(register_49_q), .in17(register_50_q),
    .in18(register_51_q), .in19(register_52_q), .in20(register_53_q), .in21(register_54_q),
    .in22(register_55_q), .in23(register_56_q), .in24(register_57_q), .in25(register_58_q),
    .in26(register_59_q), .in27(register_60_q), .in28(register_61_q), .in29(register_62_q),
    .in30(register_63_q), .in31(register_64_q), .out(ReadData4Out), .sel(ReadDataIn4));
  // Probe on ReadData1Out
endmodule
