// Logisim project VectorSimdShader.circ as structural Verilog: 3 circuits, main circuit ShaderCore
module ShaderCore (
  input  [31:0] WriteDataIn,
  input  [4:0] DataAddressInA,
  input  [4:0] DataAddressInB,
  input  [4:0] ReadDataInA,
  input  [4:0] ReadDataInB,
  input  [4:0] ReadDataInC,
  input  [4:0] ReadDataInD,
  input  regWrite,
  input  [4:0] bitShiftIn,
  input  [5:0] opCode,
  input  clearRegisters,
  input  clockIn,
  output [31:0] PortA,
  output [31:0] PortB,
  output [31:0] PortC,
  output [31:0] PortD
);

  wire [31:0] registerfile_1_readdata1out, registerfile_1_readdata2out, registerfile_1_readdata3out,
       registerfile_1_readdata4out;

  RegisterFile registerfile_1 (
    .WriteDataIn(WriteDataIn), .WriteRegInBlock1(DataAddressInA), .WriteRegInBlock2(DataAddressInB),
    .ReadDataIn1(ReadDataInA), .ReadDataIn2(ReadDataInB), .ReadDataIn3(ReadDataInC),
    .ReadDataIn4(ReadDataInD), .ClockIn(clockIn), .regWrite(regWrite),
    .ReadData1Out(registerfile_1_readdata1out), .ReadData2Out(registerfile_1_readdata2out),
    .ReadData3Out(registerfile_1_readdata3out), .ReadData4Out(registerfile_1_readdata4out));
  SimdShader simdshader_1 (
    .X0(registerfile_1_readdata1out), .Y0(registerfile_1_readdata2out), .X1(registerfile_1_readdata3out),
    .Y1(registerfile_1_readdata4out), .shiftIn(bitShiftIn), .Op(opCode), .ClearRegisters(clearRegisters),
    .clockIn(clockIn), .out_9(PortA), .out_10(PortB), .out_11(PortC), .out_12(PortD));
endmodule

module ShaderExecuteBackend (
  input  [31:0] A,
  input  [31:0] B,
  input  [5:0] Opcode,
  input  [4:0] shiftAmount,
  output [31:0] Result,
  output ErrorBit
);

  wire [31:0] fpuadder_1_floatresult, fpumul_1_fpumulresult, thirtytwobitalu_1_result;

  thirtyTwoBitALU thirtytwobitalu_1 (
    .A(A), .B(B), .Opcode(Opcode[3:0]), .shiftAmount(shiftAmount), .Result(thirtytwobitalu_1_result));  // open: ErrorBit
  FPUMul fpumul_1 (.Ain(A), .Bin(B), .FPUMulResult(fpumul_1_fpumulresult), .Overflow(ErrorBit));
  FPUAdder fpuadder_1 (.FloatSubMode(Opcode[0]), .Float32A(A), .Float32B(B), .FloatResult(fpuadder_1_floatresult));
  // Probe on thirtytwobitalu_1_result
  // Probe on Result
  Multiplexer #(.enable("false"), .select(2), .width(32)) multiplexer_1 (
    .in0(thirtytwobitalu_1_result), .in1(thirtytwobitalu_1_result), .in2(fpumul_1_fpumulresult),
    .in3(fpuadder_1_floatresult), .out(Result), .sel({Opcode[4], Opcode[5]}));
  // Probe on fpuadder_1_floatresult
  // Probe on Result
endmodule

module SimdShader (
  input  [31:0] X0,
  input  [31:0] Y0,
  input  [31:0] X1,
  input  [31:0] Y1,
  input  [4:0] shiftIn,
  input  [5:0] Op,
  input  ClearRegisters,
  input  clockIn,
  output [31:0] out_9,
  output [31:0] out_10,
  output [31:0] out_11,
  output [31:0] out_12
);

  wire [31:0] X0X1Shader_result, X0Y0Shader_result, X1Y1Shader_result, Y1Y0Shader_result;
  wire [63:0] X0Y0_q, X1Y1_q;

  Register #(.width(64)) X0Y0 (.D({Y0, X0}), .clk(clockIn), .Q(X0Y0_q), .clr(ClearRegisters));  // open: en
  Register #(.width(64)) X1Y1 (.D({Y1, X1}), .clk(clockIn), .Q(X1Y1_q), .clr(ClearRegisters));  // open: en
  ShaderExecuteBackend X0Y0Shader (
    .A(X0Y0_q[31:0]), .B(X0Y0_q[63:32]), .Opcode(Op), .shiftAmount(shiftIn), .Result(X0Y0Shader_result));  // open: ErrorBit
  ShaderExecuteBackend X0X1Shader (
    .A(X0Y0_q[31:0]), .B(X1Y1_q[31:0]), .Opcode(Op), .shiftAmount(shiftIn), .Result(X0X1Shader_result));  // open: ErrorBit
  ShaderExecuteBackend X1Y1Shader (
    .A(X1Y1_q[31:0]), .B(X1Y1_q[63:32]), .Opcode(Op), .shiftAmount(shiftIn), .Result(X1Y1Shader_result));  // open: ErrorBit
  ShaderExecuteBackend Y1Y0Shader (
    .A(X0Y0_q[63:32]), .B(X1Y1_q[63:32]), .Opcode(Op), .shiftAmount(shiftIn), .Result(Y1Y0Shader_result));  // open: ErrorBit
  Register #(.width(32)) register_1 (
    .D(X0Y0Shader_result), .clk(clockIn), .Q(out_9), .clr(ClearRegisters));  // open: en
  Register #(.width(32)) register_2 (
    .D(X0X1Shader_result), .clk(clockIn), .Q(out_10), .clr(ClearRegisters));  // open: en
  Register #(.width(32)) register_3 (
    .D(X1Y1Shader_result), .clk(clockIn), .Q(out_11), .clr(ClearRegisters));  // open: en
  Register #(.width(32)) register_4 (
    .D(Y1Y0Shader_result), .clk(clockIn), .Q(out_12), .clr(ClearRegisters));  // open: en
endmodule
